// Logisim project logisimPart2.circ as structural Verilog: 2 circuits, main circuit main
module main (
  input  [7:0] in_1,
  input  [7:0] in_2
);

  AddMachine addmachine_1 (.out_1(in_1), .out_2(in_2));
endmodule

module AddMachine (
  output [7:0] out_1,
  output [7:0] out_2
);

  wire clock_1_out;

  Adder adder_1 (.a(out_1), .b(8'h1), .out(out_2));  // open: cin, cout
  Clock clock_1 (.out(clock_1_out));
  Register register_1 (.D(out_2), .Q(out_1), .clk(clock_1_out));  // open: en, clr
endmodule
