// Logisim project alu.circ as structural Verilog: 4 circuits, main circuit main
module main (
  input  [31:0] X,
  input  [31:0] Y,
  input  Clock,
  input  Mul_Div_Reset,
  input  [5:0] Switch__S,
  output Equal,
  output Signed_Overflow,
  output [31:0] RESULT,
  output [31:0] toHi,
  output Stall_Pipeline
);

  wire add_funct, add_overflow, and_2_out, and_3_out, comparator_3_eq, comparator_9_eq, comparator_10_lt,
       comparator_11_lt, divsubu_funct, mulad_funct, multiplexer_2_out, multiplexer_3_out, not_1_out,
       not_2_out, not_3_out, same_top_bit, should_stall_divsubu, should_stall_mul, sub_funct, sub_overflow;
  wire [4:0] bit_extender_1_out, bit_extender_2_out, bit_extender_3_out;
  wire [31:0] add, adder_2_out, addu, \and , counter_1_q, divsubu, mulad, \or , register_1_q, register_2_q,
       sll, slt, sltu, sra, srl, sub, subu;

  Bit_Extender #(.in_width(32), .out_width(5)) bit_extender_1 (.in(Y), .out(bit_extender_1_out));
  Register #(.width(32)) register_1 (.D(Y), .Q(register_1_q), .clk(Mul_Div_Reset));  // open: en, clr
  Comparator #(.width(5)) comparator_1 (
    .a({Switch__S[5], Switch__S[3:0]}), .b(5'b10000), .eq(add_funct));  // open: gt, lt
  Comparator #(.width(5)) comparator_2 (
    .a({Switch__S[5], Switch__S[3:0]}), .b(5'b10010), .eq(sub_funct));  // open: gt, lt
  Subtractor #(.width(32)) subtractor_1 (.a(X), .b(Y), .out(subu));  // open: bin, bout
  assign \and  = X & Y;  // AND_Gate and_1, 32 bits wide
  Shifter #(.width(32)) shifter_1 (.in(X), .\dist (bit_extender_1_out), .out(sll));
  Adder #(.width(32)) adder_1 (.a(X), .b(Y), .out(add));  // open: cin, cout
  not not_1 (not_1_out, comparator_3_eq);
  Comparator #(.width(1)) comparator_3 (.a(X[31]), .b(add[31]), .eq(comparator_3_eq));  // open: gt, lt
  Register #(.width(32)) register_2 (.D(X), .Q(register_2_q), .clk(Mul_Div_Reset));  // open: en, clr
  Register #(.width(32)) register_3 (
    .D(adder_2_out), .en(should_stall_mul), .Q(mulad), .clk(Clock), .clr(Mul_Div_Reset));
  Counter #(.width(32), .max('hffffffff)) counter_1 (
    .count(1'b1), .Q(counter_1_q), .clk(Clock), .clr(Mul_Div_Reset));  // open: load, D, carry
  Multiplexer #(.enable("false")) multiplexer_1 (.in0(1'b0), .in1(not_1_out), .out(add_overflow), .sel(same_top_bit));
  Comparator #(.width(32)) comparator_4 (.a(counter_1_q), .b(register_1_q), .lt(should_stall_mul));  // open: gt, eq
  Comparator #(.width(5)) comparator_5 (
    .a({Switch__S[5], Switch__S[3:0]}), .b(5'b11110), .eq(mulad_funct));  // open: gt, lt
  Comparator #(.width(5)) comparator_6 (
    .a({Switch__S[5], Switch__S[3:0]}), .b({5{1'b1}}), .eq(divsubu_funct));  // open: gt, lt
  Adder #(.width(32)) adder_2 (.a(register_2_q), .b(mulad), .out(adder_2_out));  // open: cin, cout
  Adder #(.width(32)) adder_3 (.a(X), .b(Y), .out(addu));  // open: cin, cout
  assign \or  = X | Y;  // OR_Gate or_1, 32 bits wide
  Bit_Extender #(.in_width(32), .out_width(5)) bit_extender_2 (.in(Y), .out(bit_extender_2_out));
  Comparator #(.width(32)) comparator_7 (.a(X), .b(Y), .eq(Equal));  // open: gt, lt
  Comparator #(.width(1)) comparator_8 (.a(X[31]), .b(Y[31]), .eq(same_top_bit));  // open: gt, lt
  Shifter #(.width(32), .shift("lr")) shifter_2 (.in(X), .\dist (bit_extender_2_out), .out(srl));
  Multiplexer #(.enable("false")) multiplexer_2 (
    .in0(add_overflow), .in1(1'b0), .out(multiplexer_2_out), .sel(add_funct));
  Multiplexer #(.enable("false")) multiplexer_3 (
    .in0(1'b0), .in1(sub_overflow), .out(multiplexer_3_out), .sel(sub_funct));
  Comparator #(.width(1)) comparator_9 (.a(X[31]), .b(sub[31]), .eq(comparator_9_eq));  // open: gt, lt
  Comparator #(.width(32)) comparator_10 (.a(X), .b(Y), .lt(comparator_10_lt));  // open: gt, eq
  Comparator #(.width(32)) comparator_11 (.a(X), .b(Y), .lt(comparator_11_lt));  // open: gt, eq
  Bit_Extender #(.in_width(32), .out_width(5)) bit_extender_3 (.in(Y), .out(bit_extender_3_out));
  Subtractor #(.width(32)) subtractor_2 (.a(X), .b(Y), .out(sub));  // open: bin, bout
  not not_2 (not_2_out, comparator_9_eq);
  divsub divsub_1 (
    .A(X), .B(Y), .Clock(Clock), .Reset(Mul_Div_Reset), .Remainder(toHi),
    .Stall_Pipeline(should_stall_divsubu), .Quotient(divsubu));
  or or_2 (Signed_Overflow, multiplexer_2_out, multiplexer_3_out);
  Multiplexer #(.select(5), .width(32), .enable("false")) multiplexer_4 (
    .in0(sll), .in2(srl), .in3(sra), .in16(add), .in17(addu), .in18(sub), .in19(subu), .in20(\and ),
    .in21(\or ), .in26(slt), .in27(sltu), .in30(mulad), .in31(divsubu), .out(RESULT),
    .sel({Switch__S[5], Switch__S[3:0]}));  // open: in1, in4, in5, in6, in7, in8, in9, in10, in11, in12, in13, in14, in15, in22, in23, in24, in25, in28, in29
  not not_3 (not_3_out, same_top_bit);
  Multiplexer #(.enable("false")) multiplexer_5 (.in0(1'b0), .in1(not_2_out), .out(sub_overflow), .sel(not_3_out));
  assign sltu = {{31{1'b0}}, comparator_10_lt};  // Bit_Extender bit_extender_4
  assign slt = {{31{1'b0}}, comparator_11_lt};  // Bit_Extender bit_extender_5
  Shifter #(.width(32), .shift("ar")) shifter_3 (.in(X), .\dist (bit_extender_3_out), .out(sra));
  and and_2 (and_2_out, mulad_funct, should_stall_mul);
  or or_3 (Stall_Pipeline, and_2_out, and_3_out);
  and and_3 (and_3_out, should_stall_divsubu, divsubu_funct);

  // Other names for the same wires on the sheet: add_tbit = add[31]; clk = Clock; iff_equal = Equal;
  //   reset = Mul_Div_Reset; sub_tbit = sub[31]; switch[4:0] = {Switch__S[5], Switch__S[3:0]}; to_hi[31:0] = toHi;
  //   x_input[31:0] = X; y_input[31:0] = Y

  // Notes on the sheet:
  //   INPUTS to your circuit
  //   INPUT to your circuit
  //   SUBU (Subtraction Unsigned)
  //   AND (Boolean &)
  //   SLL (Shift Left Logical)
  //   # shamt -> 5 bits
  //   # Subtract's 16 if 1 at 5th bit
  //   # (Needed to fit in mux)
  //   Add Function is 16 in mex
  //   Sub Function is 18 in mux
  //   ADD (Addition)
  //   # Signed overflow if top bit is incorrectly found
  //   # If top two bits are not same, then will not overflow (sum -> 0)
  //   # If top two bits are same, different top bit for func -> overflow 
  //   MULAD (Multiply by Addition)
  //   Mulad Function is 30 in mex
  //   Divsubu Function is 31 in mux
  //   Core ALU (MIPS) Functions
  //   ADDU (Addition Unsigned)
  //   OR (Boolean |)
  //   SRL (Shift Right Logical)
  //   # shamt -> 5 bits
  //   IFF Equal Test
  //   # must extend to maintain size of commands
  //   Overflow Detection
  //   # Use splitter (from lab 6) to grab only most significant (top) bit
  //   DON'T CHANGE THE INPUTS AND OUTPUTS! IF YOU DO SO, YOU NEED TO MAKE SURE THE PINS ARE IN THE RIGHT PLACES!
  //   # Signed Overflow occurs only with add or sub 
  //   SUB (Subtraction)
  //   # Signed overflow if top bit is incorrectly found
  //   # If top two bits same, then will not overflow (diff -> 0)
  //   # If top two bits are not same, different top bit for func -> overflow 
  //   DIVSUB (Division by Subtraction)
  //   All other functions are unnecesary
  //   SLTU (Set Less Than Unsigned)
  //   SLT (Set Less Than)
  //   SRA (Shift Right Arithmatic)
  //   # shamt -> 5 bits
  //   OUTPUTS of your circuit
endmodule

module mulad_next (
  input  Reset,
  input  Clock,
  input  [31:0] Limit,
  output IsCounting
);

  wire comparator_1_eq, comparator_1_lt;
  wire [31:0] adder_1_out, register_1_q;

  Register #(.width(32)) register_1 (.D(adder_1_out), .Q(register_1_q), .clk(Clock), .clr(Reset));  // open: en
  Adder #(.width(32)) adder_1 (.a(32'h1), .b(register_1_q), .out(adder_1_out));  // open: cin, cout
  Comparator #(.width(32)) comparator_1 (
    .a(register_1_q), .b(Limit), .eq(comparator_1_eq), .lt(comparator_1_lt));  // open: gt
  or or_1 (IsCounting, comparator_1_lt, comparator_1_eq);

  // Other names for the same wires on the sheet: clk = Clock; rst = Reset

  // Notes on the sheet:
  //   INPUTS
  //   OUTPUTS
endmodule

module dibsub_next (
  input  [31:0] B,
  input  [31:0] Quotient,
  output IsCounting
);

  wire comparator_1_eq, comparator_1_gt;

  Comparator #(.width(32)) comparator_1 (.a(Quotient), .b(B), .gt(comparator_1_gt), .eq(comparator_1_eq));  // open: lt
  or or_1 (IsCounting, comparator_1_gt, comparator_1_eq);

  // Other names for the same wires on the sheet: quot[31:0] = Quotient; rt[31:0] = B

  // Notes on the sheet:
  //   INPUTS
  //   OUTPUTS
endmodule

module divsub (
  input  [31:0] A,
  input  [31:0] B,
  input  Clock,
  input  Reset,
  output [31:0] Remainder,
  output Stall_Pipeline,
  output [31:0] Quotient
);

  wire or_1_out;
  wire [31:0] adder_1_out, multiplexer_1_out, register_1_q, subtractor_1_out;

  Subtractor #(.width(32)) subtractor_1 (.a(Remainder), .b(register_1_q), .out(subtractor_1_out));  // open: bin, bout
  Register #(.width(32)) register_1 (.D(B), .en(Reset), .Q(register_1_q), .clk(Clock));  // open: clr
  Register #(.width(32)) register_2 (.D(adder_1_out), .Q(Quotient), .clk(Clock), .clr(Reset));  // open: en
  Multiplexer #(.width(32), .enable("false")) multiplexer_1 (
    .in0(subtractor_1_out), .in1(A), .out(multiplexer_1_out), .sel(Reset));
  Register #(.width(32)) register_3 (.D(multiplexer_1_out), .en(or_1_out), .Q(Remainder), .clk(Clock));  // open: clr
  or or_1 (or_1_out, Stall_Pipeline, Reset);
  dibsub_next dibsub_next_1 (.B(register_1_q), .Quotient(Remainder), .IsCounting(Stall_Pipeline));
  Adder #(.width(32)) adder_1 (.a(32'h1), .b(Quotient), .out(adder_1_out));  // open: cin, cout

  // Other names for the same wires on the sheet: clk = Clock; shouldStall = Stall_Pipeline

  // Notes on the sheet:
  //   INPUTS
  //   IMPLEMENT A/B
  //   OUTPUTS
endmodule
