// Logisim project cpu.circ as structural Verilog: 1 circuit, main circuit main
module main (
  input  [31:0] RS_READ_VALUE,
  input  [31:0] RT_READ_VALUE,
  input  [31:0] INSTRUCTION,
  input  CLOCK,
  input  RESET,
  output [31:0] Lo,
  output [31:0] Hi,
  output [31:0] t0,
  output [31:0] t1,
  output [31:0] t2,
  output [31:0] t3,
  output [4:0] RS,
  output [4:0] RT,
  output [4:0] Write_Register,
  output [31:0] RD_WRITE_VALUE,
  output RD_WRITE_ENABLE,
  output [23:0] FETCH_ADDRESS
);

  wire add_funct, add_imm_u, alu_src, and_1_out, and_2_out, and_3_out, and_4_out, and_5_out, and_imm, b_eq,
       b_not_eq, b_taken, byte_level_access, comparator_1_eq, comparator_2_lt, comparator_3_lt,
       comparator_4_lt, comparator_5_lt, comparator_6_eq, comparator_20_eq, comparator_21_eq,
       comparator_22_eq, comparator_23_eq, comparator_24_eq, comparator_25_eq, comparator_26_eq,
       comparator_27_eq, comparator_28_eq, comparator_29_lt, comparator_30_lt, comparator_31_eq,
       comparator_32_eq, comparator_33_eq, i_type, j___link, j_reg, j_type, jump, l_upp_imm, load_byte,
       load_byte_u, load_w, main_1_signed_overflow, mem_or_alu, nop_case, not_3_out, not_4_out, not_5_out,
       or_1_out, or_2_out, or_11_out, or_imm, r_type, shift_l_log, shift_r_artm, shift_r_log, shift_type,
       stall_pipeline, store_w, using_temp, zero_ext;
  wire [1:0] multiplexer_2_out;
  wire [4:0] reg_written_to;
  wire [5:0] alu_control, funct_type, multiplexer_16_out, multiplexer_17_out;
  wire [7:0] bit_extender_4_out;
  wire [15:6] immediate;
  wire [23:0] adder_1_out, adder_2_out, adder_3_out, bit_extender_1_out, j_reg_pc, jump_case_pc,
       multiplexer_1_out, multiplexer_6_out, multiplexer_15_out, nxt_prog_count;
  wire [31:0] alu_result, bit_extender_2_out, bit_extender_3_out, bit_extender_5_out, bit_extender_6_out,
       bit_extender_7_out, cpu_return, extd_imm, MEM_data_mem_out, multiplexer_7_out, multiplexer_8_out,
       multiplexer_9_out, multiplexer_10_out, multiplexer_11_out, multiplexer_12_out, multiplexer_13_out,
       read_data1, read_data2, rs_prop_reg, rt_prop_reg, tohi_val;
  wire [31:26] INSTRUCTION_t;

  Comparator #(.width(32)) comparator_1 (.a(rs_prop_reg), .b(rt_prop_reg), .eq(comparator_1_eq));  // open: gt, lt
  Adder #(.width(24)) adder_1 (.a(FETCH_ADDRESS), .b(24'h1), .out(adder_1_out));  // open: cin, cout
  Comparator #(.width(5)) comparator_2 (.a(5'b00111), .b(RS), .lt(comparator_2_lt));  // open: gt, eq
  and and_1 (and_1_out, comparator_2_lt, comparator_3_lt);
  Comparator #(.width(5)) comparator_3 (.a(RS), .b(5'b01100), .lt(comparator_3_lt));  // open: gt, eq
  Comparator #(.width(5)) comparator_4 (.a(5'b00111), .b(RT), .lt(comparator_4_lt));  // open: gt, eq
  and and_2 (and_2_out, comparator_4_lt, comparator_5_lt);
  Comparator #(.width(5)) comparator_5 (.a(RT), .b(5'b01100), .lt(comparator_5_lt));  // open: gt, eq
  not not_1 (alu_src, or_1_out);
  or or_1 (or_1_out, r_type, j_type);
  not not_2 (RD_WRITE_ENABLE, or_2_out);
  or or_2 (or_2_out, b_eq, b_not_eq, jump, j_reg);
  Comparator #(.width(6)) comparator_6 (.a(INSTRUCTION_t), .b(6'b001001), .eq(comparator_6_eq));  // open: gt, lt
  not not_3 (not_3_out, comparator_1_eq);
  Multiplexer #(.width(24), .enable("false")) multiplexer_1 (
    .in0(adder_1_out), .in1(FETCH_ADDRESS), .out(multiplexer_1_out), .sel(nop_case));
  assign bit_extender_1_out = {{8{immediate[15]}}, {immediate, funct_type}};  // Bit_Extender bit_extender_1
  Multiplexer #(.width(2), .enable("false")) multiplexer_2 (
    .in0(RT[1:0]), .in1(immediate[12:11]), .out(multiplexer_2_out), .sel(r_type));
  assign bit_extender_2_out = {{16{immediate[15]}}, {immediate, funct_type}};  // Bit_Extender bit_extender_2
  assign bit_extender_3_out = {{16{1'b0}}, {immediate, funct_type}};  // Bit_Extender bit_extender_3
  or or_3 (j_type, j___link, jump);
  Comparator #(.width(6)) comparator_7 (.a(INSTRUCTION_t), .b({6{1'b0}}), .eq(r_type));  // open: gt, lt
  Comparator #(.width(6)) comparator_8 (.a(INSTRUCTION_t), .b(6'b000010), .eq(jump));  // open: gt, lt
  Comparator #(.width(6)) comparator_9 (.a(INSTRUCTION_t), .b(6'b000011), .eq(j___link));  // open: gt, lt
  Comparator #(.width(6)) comparator_10 (.a(INSTRUCTION_t), .b(6'b000100), .eq(b_eq));  // open: gt, lt
  Comparator #(.width(6)) comparator_11 (.a(INSTRUCTION_t), .b(6'b000101), .eq(b_not_eq));  // open: gt, lt
  Comparator #(.width(6)) comparator_12 (.a(INSTRUCTION_t), .b(6'b001001), .eq(add_imm_u));  // open: gt, lt
  Comparator #(.width(6)) comparator_13 (.a(INSTRUCTION_t), .b(6'b001100), .eq(and_imm));  // open: gt, lt
  Comparator #(.width(6)) comparator_14 (.a(INSTRUCTION_t), .b(6'b001101), .eq(or_imm));  // open: gt, lt
  Comparator #(.width(6)) comparator_15 (.a(INSTRUCTION_t), .b(6'b001111), .eq(l_upp_imm));  // open: gt, lt
  Comparator #(.width(6)) comparator_16 (.a(INSTRUCTION_t), .b(6'b100000), .eq(load_byte));  // open: gt, lt
  Comparator #(.width(6)) comparator_17 (.a(INSTRUCTION_t), .b(6'b100011), .eq(load_w));  // open: gt, lt
  Comparator #(.width(6)) comparator_18 (.a(INSTRUCTION_t), .b(6'b100100), .eq(load_byte_u));  // open: gt, lt
  Comparator #(.width(6)) comparator_19 (.a(INSTRUCTION_t), .b(6'b101011), .eq(store_w));  // open: gt, lt
  Comparator #(.width(6)) comparator_20 (.a(INSTRUCTION_t), .b(6'b100000), .eq(comparator_20_eq));  // open: gt, lt
  and and_3 (and_3_out, b_eq, comparator_1_eq);
  or or_4 (b_taken, and_3_out, and_4_out);
  and and_4 (and_4_out, not_3_out, b_not_eq);
  Adder #(.width(24)) adder_2 (.a(multiplexer_1_out), .b(bit_extender_1_out), .out(adder_2_out));  // open: cin, cout
  Multiplexer #(.width(32), .enable("false")) multiplexer_3 (
    .in0(RS_READ_VALUE), .in1(read_data1), .out(rs_prop_reg), .sel(and_1_out));
  Multiplexer #(.width(32), .enable("false")) multiplexer_4 (
    .in0(RT_READ_VALUE), .in1(read_data2), .out(rt_prop_reg), .sel(and_2_out));
  Multiplexer #(.width(32), .enable("false")) multiplexer_5 (
    .in0(bit_extender_2_out), .in1(bit_extender_3_out), .out(extd_imm), .sel(zero_ext));
  Comparator #(.width(6)) comparator_21 (.a(INSTRUCTION_t), .b(6'b100011), .eq(comparator_21_eq));  // open: gt, lt
  Multiplexer #(.width(24), .enable("false")) multiplexer_6 (
    .in0(multiplexer_1_out), .in1(adder_2_out), .out(multiplexer_6_out), .sel(b_taken));
  regfile_main RegFile (
    .Read_register_1(RS[1:0]), .Read_register_2(RT[1:0]), .write_register(multiplexer_2_out),
    .write_data(cpu_return), .t0_Value(t0), .t1_Value(t1), .t2_Value(t2), .t3_Value(t3),
    .RegWrite(and_5_out), .clock(CLOCK), .Read_Data_1(read_data1), .Read_Data_2(read_data2));
  and and_5 (and_5_out, RD_WRITE_ENABLE, using_temp);
  mem_main MEM (
    .Data_Mem_Addr(alu_result), .Data_Mem_In(rt_prop_reg), .ACCESS_BYTE(byte_level_access),
    .MEM_WRITE(store_w), .CLOCK(CLOCK), .Data_Mem_Out(MEM_data_mem_out));
  Comparator #(.width(6)) comparator_22 (.a(INSTRUCTION_t), .b(6'b100100), .eq(comparator_22_eq));  // open: gt, lt
  Comparator #(.width(6)) comparator_23 (.a(INSTRUCTION_t), .b(6'b101011), .eq(comparator_23_eq));  // open: gt, lt
  Multiplexer #(.width(32), .enable("false")) multiplexer_7 (
    .in0(INSTRUCTION), .in1({32{1'b0}}), .out(multiplexer_7_out), .sel(nop_case));
  Multiplexer #(.width(32), .enable("false")) multiplexer_8 (
    .in0(rt_prop_reg), .in1(extd_imm), .out(multiplexer_8_out), .sel(alu_src));
  Bit_Extender #(.in_width(32), .out_width(8)) bit_extender_4 (.in(MEM_data_mem_out), .out(bit_extender_4_out));
  or or_5 (zero_ext, and_imm, or_imm);
  or or_6 (byte_level_access, load_byte, load_byte_u);
  or or_7 (i_type, comparator_6_eq, comparator_20_eq, comparator_21_eq, comparator_22_eq, comparator_23_eq);
  Register #(.width(32)) register_1 (
    .D(multiplexer_7_out), .en(not_4_out), .Q({INSTRUCTION_t, RS, RT, immediate, funct_type}), .clk(CLOCK));  // open: clr
  not not_4 (not_4_out, stall_pipeline);
  Multiplexer #(.width(32), .enable("false")) multiplexer_9 (
    .in0(rs_prop_reg), .in1(multiplexer_8_out), .out(multiplexer_9_out), .sel(l_upp_imm));
  Multiplexer #(.width(32), .enable("false")) multiplexer_10 (
    .in0(multiplexer_8_out), .in1(32'h10), .out(multiplexer_10_out), .sel(l_upp_imm));
  assign bit_extender_5_out = {{24{bit_extender_4_out[7]}}, bit_extender_4_out};  // Bit_Extender bit_extender_5
  not not_5 (not_5_out, stall_pipeline);
  Multiplexer #(.width(32), .enable("false")) multiplexer_11 (
    .in0(multiplexer_9_out), .in1(rt_prop_reg), .out(multiplexer_11_out), .sel(shift_type));
  Multiplexer #(.width(32), .enable("false")) multiplexer_12 (
    .in0(multiplexer_10_out), .in1(bit_extender_6_out), .out(multiplexer_12_out), .sel(shift_type));
  Multiplexer #(.width(32), .enable("false")) multiplexer_13 (
    .in0(MEM_data_mem_out), .in1(bit_extender_5_out), .out(multiplexer_13_out), .sel(load_byte));
  Multiplexer #(.width(5), .enable("false")) multiplexer_14 (
    .in0(RT), .in1(immediate[15:11]), .out(reg_written_to), .sel(r_type));
  Adder #(.width(24)) adder_3 (.a(FETCH_ADDRESS), .b(24'h100000), .out(adder_3_out));  // open: cin, cout
  Multiplexer #(.width(24), .enable("false")) multiplexer_15 (
    .in0(multiplexer_6_out), .in1(jump_case_pc), .out(multiplexer_15_out), .sel(j_type));
  assign bit_extender_6_out = {{27{1'b0}}, immediate[10:6]};  // Bit_Extender bit_extender_6
  Comparator #(.width(6)) comparator_24 (.a({6{1'b0}}), .b(funct_type), .eq(comparator_24_eq));  // open: gt, lt
  Comparator #(.width(6)) comparator_25 (.a(6'b000010), .b(funct_type), .eq(comparator_25_eq));  // open: gt, lt
  Comparator #(.width(6)) comparator_26 (.a(6'b000011), .b(funct_type), .eq(comparator_26_eq));  // open: gt, lt
  Comparator #(.width(6)) comparator_27 (.a(funct_type), .b(6'b001000), .eq(comparator_27_eq));  // open: gt, lt
  Comparator #(.width(6)) comparator_28 (.a(funct_type), .b(6'b100000), .eq(comparator_28_eq));  // open: gt, lt
  Multiplexer #(.width(6), .enable("false")) multiplexer_16 (
    .in0(multiplexer_17_out), .in1(6'b100001), .out(multiplexer_16_out), .sel(i_type));
  Multiplexer #(.width(6), .enable("false")) multiplexer_17 (
    .in0(6'b100101), .in1({6{1'b0}}), .out(multiplexer_17_out), .sel(l_upp_imm));
  Multiplexer #(.width(5), .enable("false")) multiplexer_18 (
    .in0(reg_written_to), .in1({5{1'b1}}), .out(Write_Register), .sel(j___link));
  assign bit_extender_7_out = {{8{1'b0}}, adder_3_out};  // Bit_Extender bit_extender_7
  Register #(.width(24)) register_2 (.D(nxt_prog_count), .en(not_5_out), .Q(FETCH_ADDRESS), .clk(CLOCK));  // open: clr
  Subtractor #(.width(24)) subtractor_1 (
    .a({RS[2:0], RT, immediate, funct_type}), .b(24'h100000), .out(jump_case_pc));  // open: bin, bout
  Subtractor #(.width(24)) subtractor_2 (.a(rs_prop_reg[23:0]), .b(24'h100000), .out(j_reg_pc));  // open: bin, bout
  Multiplexer #(.width(24), .enable("false")) multiplexer_19 (
    .in0(multiplexer_15_out), .in1(j_reg_pc), .out(nxt_prog_count), .sel(j_reg));
  Comparator #(.width(5)) comparator_29 (.a(5'b00111), .b(reg_written_to), .lt(comparator_29_lt));  // open: gt, eq
  Comparator #(.width(5)) comparator_30 (.a(reg_written_to), .b(5'b01100), .lt(comparator_30_lt));  // open: gt, eq
  LED led_1 (.in(main_1_signed_overflow));
  alu_main main_1 (
    .Switch__S(alu_control), .X(multiplexer_11_out), .RESULT(alu_result),
    .Signed_Overflow(main_1_signed_overflow), .Y(multiplexer_12_out), .toHi(tohi_val),
    .Stall_Pipeline(stall_pipeline), .Clock(CLOCK), .Mul_Div_Reset(RESET));  // open: Equal
  Multiplexer #(.width(32), .enable("false")) multiplexer_20 (
    .in0(alu_result), .in1(multiplexer_13_out), .out(cpu_return), .sel(mem_or_alu));
  and and_6 (shift_l_log, r_type, comparator_24_eq);
  and and_7 (shift_r_log, r_type, comparator_25_eq);
  and and_8 (shift_r_artm, r_type, comparator_26_eq);
  and and_9 (j_reg, r_type, comparator_27_eq);
  and and_10 (add_funct, r_type, comparator_28_eq);
  Multiplexer #(.width(6), .enable("false")) multiplexer_21 (
    .in0(multiplexer_16_out), .in1(funct_type), .out(alu_control), .sel(comparator_33_eq));
  Multiplexer #(.width(32), .enable("false")) multiplexer_22 (
    .in0(cpu_return), .in1(bit_extender_7_out), .out(RD_WRITE_VALUE), .sel(j___link));
  or or_8 (nop_case, j_type, b_taken);
  and and_11 (using_temp, comparator_29_lt, comparator_30_lt);
  Comparator #(.width(6)) comparator_31 (.a(alu_control), .b(6'b111110), .eq(comparator_31_eq));  // open: gt, lt
  Comparator #(.width(6)) comparator_32 (.a(alu_control), .b({6{1'b1}}), .eq(comparator_32_eq));  // open: gt, lt
  or or_9 (shift_type, shift_l_log, shift_r_log, shift_r_artm);
  or or_10 (mem_or_alu, load_byte, load_w, load_byte_u);
  or or_11 (or_11_out, comparator_31_eq, comparator_32_eq);
  Register #(.width(32)) u_Hi (.D(tohi_val), .en(comparator_32_eq), .Q(Hi), .clk(CLOCK));  // open: clr
  Comparator #(.width(6)) comparator_33 (.a(INSTRUCTION_t), .b({6{1'b0}}), .eq(comparator_33_eq));  // open: gt, lt
  Register #(.width(32)) u_Lo (.D(alu_result), .en(or_11_out), .Q(Lo), .clk(CLOCK));  // open: clr

  // Other names for the same wires on the sheet: clk = CLOCK; immediate[5:0] = funct_type;
  //   INSTRUCTION_t[25:0] = {RS, RT, immediate, funct_type}; j_type_addr[25:0] = {RS, RT, immediate, funct_type};
  //   shamt[4:0] = immediate[10:6]; rd_reg[4:0] = immediate[15:11]; rt_reg[4:0] = RT; rs_reg[4:0] = RS;
  //   opcode[5:0] = INSTRUCTION_t; fetch_addr[23:0] = FETCH_ADDRESS; prog_count[23:0] = FETCH_ADDRESS;
  //   RS_VAL[31:0] = RS_READ_VALUE; rst = RESET; RT_VAL[31:0] = RT_READ_VALUE; write_enable = RD_WRITE_ENABLE;
  //   write_from_mem = store_w; write_reg[4:0] = Write_Register; write_value[31:0] = RD_WRITE_VALUE

  // Notes on the sheet:
  //   # Increment PC if not branch (not nop)
  //   # ALUSrc true when I-type funct
  //   # If branch taken, add imm addr to PC (extend - MIPS sheet)
  //   # Only need 2 bits (mux chooses t regs)
  //   # To account for Regfile's 4 registers ($t0 - $t3)
  //   # Check if rs and rt are temps, use appropriate values
  //   # All load/store use $rt for return
  //   # No write if your're jumping/branching
  //   # (Jal doesn't count, cause we must write)
  //   These are outputs/inputs from run.circ
  //   1) Determine branch value to set next PC value
  //   A) Find if branch is taken (case is true)
  //   B) Calculate the actual branch value for the next PC
  //   # Extend imm appropriately (only andi / ori 0-extd)
  //   #I-type opcodes (addiu, lb, lw, lbu, and sw respectively from top to bottom
  //   # Use nop for J or I type
  //   # J-type funct
  //   # Place all appropriate inputs for mem circuit
  //   PC Value Adjustments
  //   # Use branch value unless jump case
  //   Core Steps for the CPU
  //   I) Split the instruction into parts
  //   # I-type funct
  //   II) Call the Regfile step with all appropriate inputs/outputs
  //   III) Use Regfile inputs and determine ALU inputs
  //   # Call to lui causes 16 bit shift (Also uses only $rt values)
  //   # ALUSrc determines immediate or register to be used
  //   IV) Access memory and determine what value should be written
  //   # SPECIAL CASE: Load Byte (Errored while testing)
  //   # Must 0 extend then sign extend to extend most significant bit across 32 bits
  //   Function Selection
  //   (Splits functions by opcode)
  //   Variable Selection
  //   (Selects when a control variable should be high based on function opcodes)
  //   # Only andi and ori are zero-extended (from MIPS sheet)
  //   # Helps us deal with byte cases (in mem.circ)
  //   ALU Control (Switch)
  //   # Account for shift details (uses stardard rt val)
  //   # Adjust for base addr (Remember: byte-addressed)
  //   # Grab next PC value (on clock cycle)
  //   # Store the instruction value for future
  //   # R-type funct
  //   These are outputs to run.circ
  //   # Only jal will write to the $ra regt.
  //   2) Find the next PC value based on instrcts called
  //   # If reg is $t0 - $t3
  //   # Specific R-type functions (only necessary ones listed)
  //   # Adjust for base addr (Remember: byte-addressed)
  //   # Must be only 24 bits for PC
  //   Use rs reg (to store address) for JR funct
  //   # Find appropriate next PC value
  //   # If writing from memory, use updated result
  //   # Jal sets $ra to the next instruction after PC
  //   # Set PC value on next clock cycle
  //   # No op when branch taken or jump called
  //   # Store the value of Lo and Hi only when appropriate
  //   # When mem called, data mem:
  //   # (1) high = store / (2) low = load
  //   # Save data mem to regs if loading
  //   #checks if it is a funct vs opcode
endmodule
