// Logisim project mem.circ as structural Verilog: 1 circuit, main circuit main
module main (
  input  [31:0] Data_Mem_Addr,
  input  [31:0] Data_Mem_In,
  input  ACCESS_BYTE,
  input  MEM_WRITE,
  input  CLOCK,
  output [31:0] Data_Mem_Out
);

  wire not_1_out;
  wire [1:0] det_addr;
  wire [7:0] multiplexer_1_out;
  wire [31:0] bit_extender_1_out, ret;
  wire [31:2] subtractor_1_out;

  Subtractor #(.width(32)) subtractor_1 (
    .a(Data_Mem_Addr), .b(32'h10010000), .out({subtractor_1_out, det_addr}));  // open: bin, bout
  Multiplexer #(.select(2), .width(8), .enable("false")) multiplexer_1 (
    .in0(ret[7:0]), .in1(ret[15:8]), .in2(ret[23:16]), .in3(ret[31:24]), .out(multiplexer_1_out),
    .sel(det_addr));
  assign bit_extender_1_out = {{24{1'b0}}, multiplexer_1_out};  // Bit_Extender bit_extender_1
  not not_1 (not_1_out, MEM_WRITE);
  RAM #(.addrWidth(24), .dataWidth(32), .bus("separate")) ram_1 (
    .addr(subtractor_1_out[25:2]), .din(Data_Mem_In), .data(ret), .str(MEM_WRITE), .sel(1'b1), .clk(CLOCK),
    .ld(not_1_out), .clr(1'b0));
  Multiplexer #(.width(32), .enable("false")) multiplexer_2 (
    .in0(bit_extender_1_out), .in1(ret), .out(Data_Mem_Out), .sel(ACCESS_BYTE));

  // Other names for the same wires on the sheet: access = ACCESS_BYTE

  // Notes on the sheet:
  //   These are INPUTS to the circuit
  //   # Base addr adjsmt. (normalize)
  //   # Last 2 bits determine word addr (0-3)
  //   These are INPUTS to the circuit
  //   DO NOT CHANGE THE LOCATIONS OF THE INPUTS/OUTPUTS! IF YOU DO SO, YOU NEED TO MAKE SURE THE PINS ARE AT THE RIGHT PLACE!
  //   # Lost bits (26-31)
  //   # Byte stored in least signf. (bottom) byte of data out
  //   # (Only if lb, not if lw/sw)
  //   # Big endian split ("standard" way to split)
  //   Yet again, the clock is not an actual clock, but an input, one that will be driven from a higher circuit
  //   # Write only if mem_write is true
  //   # Seperate read/write (failed otherwise)
  //   # If lb, load extended byte
  //   # If lw/sw, use full data (ret)
  //   This is an OUTPUT to the circuit
endmodule
