// Logisim project regfile.circ as structural Verilog: 1 circuit, main circuit main
module main (
  input  [1:0] Read_register_1,
  input  [1:0] Read_register_2,
  input  [1:0] write_register,
  input  [31:0] write_data,
  input  RegWrite,
  input  clock,
  output [31:0] t0_Value,
  output [31:0] t1_Value,
  output [31:0] t2_Value,
  output [31:0] t3_Value,
  output [31:0] Read_Data_1,
  output [31:0] Read_Data_2
);

  wire demultiplexer_1_out0, demultiplexer_1_out1, demultiplexer_1_out2, demultiplexer_1_out3, not_1_out,
       not_2_out, not_3_out, not_4_out;
  wire [31:0] multiplexer_1_out, multiplexer_2_out, multiplexer_3_out, multiplexer_4_out;

  Multiplexer #(.width(32)) multiplexer_1 (
    .in0(write_data), .in1(t0_Value), .out(multiplexer_1_out), .sel(not_1_out), .en(RegWrite));
  Multiplexer #(.width(32)) multiplexer_2 (
    .in0(write_data), .in1(t1_Value), .out(multiplexer_2_out), .sel(not_2_out), .en(RegWrite));
  Demultiplexer #(.select(2), .enable("false")) demultiplexer_1 (
    .out0(demultiplexer_1_out0), .out1(demultiplexer_1_out1), .out2(demultiplexer_1_out2),
    .out3(demultiplexer_1_out3), .in(1'b1), .sel(write_register));
  Register #(.width(32)) register_1 (.D(multiplexer_1_out), .Q(t0_Value), .clk(clock));  // open: en, clr
  Register #(.width(32)) register_2 (.D(multiplexer_2_out), .Q(t1_Value), .clk(clock));  // open: en, clr
  not not_1 (not_1_out, demultiplexer_1_out0);
  not not_2 (not_2_out, demultiplexer_1_out1);
  not not_3 (not_3_out, demultiplexer_1_out2);
  not not_4 (not_4_out, demultiplexer_1_out3);
  Multiplexer #(.width(32)) multiplexer_3 (
    .in0(write_data), .in1(t2_Value), .out(multiplexer_3_out), .sel(not_3_out), .en(RegWrite));
  Multiplexer #(.width(32)) multiplexer_4 (
    .in0(write_data), .in1(t3_Value), .out(multiplexer_4_out), .sel(not_4_out), .en(RegWrite));
  Register #(.width(32)) register_3 (.D(multiplexer_3_out), .Q(t2_Value), .clk(clock));  // open: en, clr
  Register #(.width(32)) register_4 (.D(multiplexer_4_out), .Q(t3_Value), .clk(clock));  // open: en, clr
  Multiplexer #(.select(2), .width(32), .enable("false")) multiplexer_5 (
    .in0(t0_Value), .in1(t1_Value), .in2(t2_Value), .in3(t3_Value), .out(Read_Data_1), .sel(Read_register_1));
  Multiplexer #(.select(2), .width(32), .enable("false")) multiplexer_6 (
    .in0(t0_Value), .in1(t1_Value), .in2(t2_Value), .in3(t3_Value), .out(Read_Data_2), .sel(Read_register_2));

  // Other names for the same wires on the sheet: write = RegWrite

  // Notes on the sheet:
  //   These are INPUTS to the circuit
  //   These are INPUTS to the circuit
  //   DO NOT CHANGE THE LOCATIONS OF THE INPUTS/OUTPUTS! IF YOU DO SO, YOU NEED TO MAKE SURE THE PINS ARE AT THE RIGHT PLACE!
  //   These are OUTPUTS to the circuit
  //   Yet again, the clock is not an actual clock, but an input, one that will be driven from a higher circuit
  //   These are OUTPUTS to the circuit
endmodule
