// Logisim project ALU-divsub.circ as structural Verilog: 1 circuit, main circuit main
module main (
  output [7:0] Test_num,
  output Equal,
  output Signed_Overflow,
  output [31:0] Result,
  output [31:0] toHi,
  output Stall_Pipeline
);

  wire Clock, rom_4_data;
  wire [5:0] rom_3_data;
  wire [7:0] adder_1_out;
  wire [31:0] rom_1_data, rom_2_data;

  Clock clock_1 (.out(Clock));
  Adder adder_1 (.a(8'h1), .b(Test_num), .out(adder_1_out));  // open: cin, cout
  Register register_1 (.D(adder_1_out), .Q(Test_num), .clk(Clock));  // open: en, clr
  ROM #(.dataWidth(32)) rom_1 (.addr(Test_num), .data(rom_1_data));  // open: sel
  ROM #(.dataWidth(32)) rom_2 (.addr(Test_num), .data(rom_2_data));  // open: sel
  ROM #(.dataWidth(6)) rom_3 (.addr(Test_num), .data(rom_3_data));  // open: sel
  ROM #(.dataWidth(1)) rom_4 (.addr(Test_num), .data(rom_4_data));  // open: sel
  alu_main main_1 (
    .Switch__S(rom_3_data), .X(rom_1_data), .Equal(Equal), .RESULT(Result),
    .Signed_Overflow(Signed_Overflow), .Y(rom_2_data), .toHi(toHi), .Stall_Pipeline(Stall_Pipeline),
    .Clock(Clock), .Mul_Div_Reset(rom_4_data));

  // Notes on the sheet:
  //   contents of rom_1 (hex, n*v repeats v):
  //   a 6*0 8
  //   contents of rom_2 (hex, n*v repeats v):
  //   3 6*0 2
  //   contents of rom_3 (hex, n*v repeats v):
  //   3f 6*0 3f
  //   contents of rom_4 (hex, n*v repeats v):
  //   1 6*0 1
  //   YOUR ALU SHOULD FIT HERE
  //   There should be no blue/red wires here, and the result shouldn't be x's.
endmodule
